// Logisim project main.circ as structural Verilog: 4 circuits, main circuit TwoBitAdder
module TwoBitAdder (
  input  [1:0] A,
  input  [1:0] B,
  input  C_in,
  output [1:0] Sum,
  output C_out
);

  wire and_1_out, and_2_out, and_3_out, and_4_out, or_1_out, xor_1_out, xor_3_out;

  xor xor_1 (xor_1_out, A[0], B[0]);
  xor xor_2 (Sum[0], xor_1_out, C_in);
  and and_1 (and_1_out, xor_1_out, C_in);
  and and_2 (and_2_out, A[0], B[0]);
  or or_1 (or_1_out, and_1_out, and_2_out);
  xor xor_3 (xor_3_out, A[1], B[1]);
  xor xor_4 (Sum[1], xor_3_out, or_1_out);
  and and_3 (and_3_out, xor_3_out, or_1_out);
  and and_4 (and_4_out, A[1], B[1]);
  or or_2 (C_out, and_3_out, and_4_out);

  // Notes on the sheet:
  //   External Carry
  //   S1
  //   Two Bit Adder
  //   B1
  //   B2
  //   S2
  //   Carry-out
endmodule

module FourBitAdder (
  input  [3:0] A,
  input  [3:0] B,
  input  C_in,
  output [3:0] Sum,
  output C_out
);

  wire twobitadder_1_c_out;

  TwoBitAdder twobitadder_1 (.A(A[1:0]), .B(B[1:0]), .C_in(C_in), .Sum(Sum[1:0]), .C_out(twobitadder_1_c_out));
  TwoBitAdder twobitadder_2 (.A(A[3:2]), .B(B[3:2]), .C_in(twobitadder_1_c_out), .Sum(Sum[3:2]), .C_out(C_out));
endmodule

module EightBitAdder (
  input  [7:0] A,
  input  [7:0] B,
  input  C_in,
  output [7:0] Sum,
  output C_out
);

  wire fourbitadder_1_c_out;

  FourBitAdder fourbitadder_1 (.A(A[3:0]), .B(B[3:0]), .C_in(C_in), .Sum(Sum[3:0]), .C_out(fourbitadder_1_c_out));
  FourBitAdder fourbitadder_2 (.A(A[7:4]), .B(B[7:4]), .C_in(fourbitadder_1_c_out), .Sum(Sum[7:4]), .C_out(C_out));
endmodule

module SixteenBitAdder (
  input  [15:0] A,
  input  [15:0] B,
  input  C_in,
  output [15:0] Sum,
  output C_out
);

  wire eightbitadder_1_c_out;

  EightBitAdder eightbitadder_1 (.A(A[7:0]), .B(B[7:0]), .C_in(C_in), .Sum(Sum[7:0]), .C_out(eightbitadder_1_c_out));
  EightBitAdder eightbitadder_2 (
    .A(A[15:8]), .B(B[15:8]), .C_in(eightbitadder_1_c_out), .Sum(Sum[15:8]), .C_out(C_out));
endmodule
